# Fritzing sketch selfmadecul (saved by Fritzing 0.9.3b)
circuit board: 3.01996cm x 9.72079cm
breadboards: 1

parts:
  Bauteil1 = Arduino Nano (Rev3.0)
  J1 = female pin header, 8 pins [form="♀ (female)"]
  R1 = Resistor [tolerance=±5% resistance=220 package=THT]
  LED1 = LED - 5mm [color="Red (633nm)" package="5 mm [THT]"]
  R2 = Resistor [tolerance=±5% resistance=420 package=THT]
  R3 = Resistor [tolerance=±5% resistance=1k package=THT]
  R4 = Resistor [tolerance=±5% resistance=420 package=THT]
  R5 = Resistor [tolerance=±5% resistance=1k package=THT]
  R6 = Resistor [tolerance=±5% resistance=420 package=THT]
  R7 = Resistor [tolerance=±5% resistance=1k package=THT]
  R8 = Resistor [tolerance=±5% resistance=10k package=THT]

nets:
  GND: Bauteil1.GND, J1.pin2, LED1.cathode, R3.Pin_1, R5.Pin_1, R7.Pin_1
  GDO2: Bauteil1.D2, J1.pin6
  GDO0: Bauteil1.D3, J1.pin7
  N1: Bauteil1.D9, R1.Pin_0
  N2: Bauteil1.D10, R6.Pin_0
  N3: Bauteil1.D11/MOSI, R2.Pin_0
  MISO: Bauteil1.D12/MISO, J1.pin5
  3.3V: Bauteil1.3V3, J1.pin1, R8.Pin_0
  N4: Bauteil1.D13/SCK, R4.Pin_0
  MOSI: J1.pin3, R2.Pin_1, R3.Pin_0
  SCLK: J1.pin4, R4.Pin_1, R5.Pin_0
  CSN: J1.pin8, R6.Pin_1, R7.Pin_0, R8.Pin_1
  N5: R1.Pin_1, LED1.anode
